// Logisim project AIU.circ as structural Verilog: 1 circuit, main circuit main
module main (
  input  in_1,
  input  in_2,
  input  [1:0] in_3,
  input  in_4,
  input  in_5,
  input  in_6,
  input  in_7,
  input  in_8,
  input  in_9,
  input  in_10,
  input  in_11,
  input  in_12,
  output out_13,
  output out_14,
  output out_15,
  output out_16
);

  wire adder_4_cout, multiplexer_1_out, multiplexer_2_out, multiplexer_3_out, multiplexer_4_out, not_1_out,
       not_2_out, not_3_out, not_4_out, not_5_out;

  not not_1 (not_1_out, in_5);
  not not_2 (not_2_out, in_7);
  not not_3 (not_3_out, in_9);
  not not_4 (not_4_out, in_11);
  not not_5 (not_5_out, in_1);
  Multiplexer #(.select(2)) multiplexer_1 (
    .in0(in_5), .in1(not_1_out), .in2(in_1), .in3(not_5_out), .out(multiplexer_1_out), .sel(in_3));  // open: en
  Multiplexer #(.select(2)) multiplexer_2 (
    .in0(in_7), .in1(not_2_out), .in2(in_1), .in3(not_5_out), .out(multiplexer_2_out), .sel(in_3));  // open: en
  Multiplexer #(.select(2)) multiplexer_3 (
    .in0(in_9), .in1(not_3_out), .in2(in_1), .in3(not_5_out), .out(multiplexer_3_out), .sel(in_3));  // open: en
  Multiplexer #(.select(2)) multiplexer_4 (
    .in0(in_11), .in1(not_4_out), .in2(in_1), .in3(not_5_out), .out(multiplexer_4_out), .sel(in_3));  // open: en
  Adder #(.width(1)) adder_1 (.a(in_4), .b(multiplexer_1_out), .out(out_13), .cin(in_2));  // open: cout
  Adder #(.width(1)) adder_2 (.a(in_6), .b(multiplexer_2_out), .out(out_14));  // open: cin, cout
  Adder #(.width(1)) adder_3 (.a(in_8), .b(multiplexer_3_out), .out(out_15));  // open: cin, cout
  Adder #(.width(1)) adder_4 (.a(in_10), .b(multiplexer_4_out), .out(out_16), .cout(adder_4_cout));  // open: cin
endmodule
