// Logisim project COMMUTATIVE.circ as structural Verilog: 1 circuit, main circuit main
module main (
  input  A,
  input  A_2,
  input  B,
  input  B_2,
  output A_B,
  output A_B_2,
  output B_A,
  output B_A_2
);

  or or_1 (A_B, A, B);
  or or_2 (B_A, B, A);
  and and_1 (A_B_2, A_2, B_2);
  and and_2 (B_A_2, B_2, A_2);

  // Notes on the sheet:
  //   A
  //   B
  //   B
  //   A
  //   SL GOWTHAM 
  //   23AD041
  //   A
  //   B
  //   B
  //   A
endmodule
