// Logisim project DEMORGANS1.circ as structural Verilog: 1 circuit, main circuit main
module main (
  input  A,
  input  A_2,
  input  B,
  input  B_2,
  output A_prime_B_prime,
  output A_prime_B_prime_2,
  output AB__prime,
  output AB__prime_2
);

  wire and_1_out, and_2_out, not_1_out, not_2_out, not_4_out, not_5_out;

  not not_1 (not_1_out, A);
  or or_1 (A_prime_B_prime, not_1_out, not_2_out);
  not not_2 (not_2_out, B);
  and and_1 (and_1_out, A, B);
  not not_3 (AB__prime, and_1_out);
  not not_4 (not_4_out, A_2);
  not not_5 (not_5_out, B_2);
  or or_2 (A_prime_B_prime_2, not_4_out, not_5_out);
  and and_2 (and_2_out, A_2, B_2);
  not not_6 (AB__prime_2, and_2_out);

  // Notes on the sheet:
  //   A'
  //   B'
  //   S L GOWTHAM
  //   AB
  //   23AD041
  //   A'
  //   B'
  //   AB
endmodule
