// Logisim project DEMORGANS2.circ as structural Verilog: 1 circuit, main circuit main
module main (
  input  A,
  input  A_2,
  input  B,
  input  B_2,
  output out_5,
  output out_6,
  output A_B__prime,
  output A_B__prime_2
);

  wire not_1_out, not_2_out, not_4_out, not_5_out, or_1_out, or_2_out;

  not not_1 (not_1_out, A);
  not not_2 (not_2_out, B);
  and and_1 (out_5, not_1_out, not_2_out);
  or or_1 (or_1_out, A, B);
  not not_3 (A_B__prime, or_1_out);
  not not_4 (not_4_out, A_2);
  not not_5 (not_5_out, B_2);
  and and_2 (out_6, not_4_out, not_5_out);
  or or_2 (or_2_out, A_2, B_2);
  not not_6 (A_B__prime_2, or_2_out);

  // Notes on the sheet:
  //   A'
  //   B'
  //   A
  //   B
  //   SL GOWTHAM
  //   A'.B'
  //   A+B
  //   23AD041
  //   A'
  //   B'
  //   A
  //   B
  //   A'.B'
  //   A+B
endmodule
