// Logisim project DEMUX.circ as structural Verilog: 1 circuit, main circuit main
module main (
  input  _1,
  input  _0,
  input  D,
  output _0_2,
  output _1_2,
  output _2,
  output _3
);

  wire not_1_out, not_2_out;

  not not_1 (not_1_out, _1);
  not not_2 (not_2_out, _0);
  and and_1 (_0_2, not_1_out, not_2_out, D);
  and and_2 (_1_2, not_1_out, _0, D);
  and and_3 (_2, _1, not_2_out, D);
  and and_4 (_3, _1, _0, D);

  // Notes on the sheet:
  //   S
  //   S
  //   SL GOWTHAM
  //   in
  //   Y
  //   23AD041
  //   Y
  //   Y
  //   Y
endmodule
