// Logisim project DFLIPFLOP.circ as structural Verilog: 1 circuit, main circuit main
module main (
  input  in_1,
  output out_2,
  output out_3
);

  wire clock_1_out, nand_1_out, nand_2_out, nand_3_out;

  Clock clock_1 (.out(clock_1_out));
  nand nand_1 (nand_1_out, in_1, clock_1_out);
  nand nand_2 (nand_2_out, in_1, in_1);
  nand nand_3 (nand_3_out, clock_1_out, nand_2_out);
  nand nand_4 (out_2, nand_1_out, out_3);
  nand nand_5 (out_3, out_2, nand_3_out);

  // Notes on the sheet:
  //   CLK
  //   SL GOWTHAM
  //   23AD041
endmodule
