// Logisim project DISTRIBUTIVE1.circ as structural Verilog: 1 circuit, main circuit main
module main (
  input  A,
  input  A_2,
  input  B,
  input  B_2,
  input  C,
  input  C_2,
  output A_B_C,
  output A_B_C_2,
  output A_B__A_C,
  output A_B__A_C_2
);

  wire and_1_out, and_3_out, or_2_out, or_3_out, or_5_out, or_6_out;

  and and_1 (and_1_out, B, C);
  or or_1 (A_B_C, A, and_1_out);
  or or_2 (or_2_out, A, B);
  or or_3 (or_3_out, A, C);
  and and_2 (A_B__A_C, or_2_out, or_3_out);
  and and_3 (and_3_out, B_2, C_2);
  or or_4 (A_B_C_2, A_2, and_3_out);
  or or_5 (or_5_out, A_2, B_2);
  or or_6 (or_6_out, A_2, C_2);
  and and_4 (A_B__A_C_2, or_5_out, or_6_out);

  // Notes on the sheet:
  //   SL GOWTHAM
  //   B
  //   23AD041
  //   C
  //   A
  //   B
  //   A
  //   C
  //   A
  //   B.C
  //   A+B
  //   A+C
  //   B
  //   C
  //   A
  //   B
  //   A
  //   C
  //   A
  //   B.C
  //   A+B
  //   A+C
endmodule
