// Logisim project DISTRIBUTIVE2.circ as structural Verilog: 1 circuit, main circuit main
module main (
  input  A,
  input  A_2,
  input  B,
  input  B_2,
  input  C,
  input  C_2,
  output A__B_C,
  output A__B_C_2,
  output A_B_A_C,
  output A_B_A_C_2
);

  wire and_2_out, and_3_out, and_4_out, and_5_out, or_1_out, or_3_out;

  or or_1 (or_1_out, B, C);
  and and_1 (A__B_C, A, or_1_out);
  and and_2 (and_2_out, A, B);
  and and_3 (and_3_out, A, C);
  or or_2 (A_B_A_C, and_2_out, and_3_out);
  or or_3 (or_3_out, B_2, C_2);
  and and_4 (and_4_out, A_2, B_2);
  and and_5 (and_5_out, A_2, C_2);
  and and_6 (A__B_C_2, A_2, or_3_out);
  or or_4 (A_B_A_C_2, and_4_out, and_5_out);

  // Notes on the sheet:
  //   B
  //   C
  //   A
  //   B
  //   A
  //   C
  //   A
  //   B+C
  //   A.B
  //   A.C
  //   SL GOWTHAM 
  //   23AD041
  //   B
  //   C
  //   A
  //   A
  //   B+C
  //   A
  //   A.B
  //   B
  //   A.C
  //   C
endmodule
