// Logisim project FULLADDER.circ as structural Verilog: 1 circuit, main circuit main
module main (
  input  A,
  input  B,
  input  C,
  output SUM,
  output CARRY
);

  wire and_1_out, and_2_out, and_3_out, or_1_out, xor_1_out;

  xor xor_1 (xor_1_out, A, B);
  and and_1 (and_1_out, A, B);
  and and_2 (and_2_out, A, C);
  and and_3 (and_3_out, B, C);
  xor xor_2 (SUM, xor_1_out, C);
  or or_1 (or_1_out, and_1_out, and_2_out);
  or or_2 (CARRY, or_1_out, and_3_out);

  // Notes on the sheet:
  //   A
  //   B
  //   SL GOWTHAM
  //   23AD041
  //   A
  //   B
  //   A
  //   C
  //   B
  //   C
  //   AB'+A'B
  //   C
  //   A.B
  //   A.C
  //   A.B+A.C
  //   B.C
endmodule
