// Logisim project HALFADDER.circ as structural Verilog: 1 circuit, main circuit main
module main (
  input  A,
  input  B,
  output SUM,
  output CARRY
);

  xor xor_1 (SUM, A, B);
  and and_1 (CARRY, A, B);

  // Notes on the sheet:
  //   A
  //   B
  //   A
  //   B
  //   SL GOWTHAM
  //   23AD041
endmodule
