// Logisim project JK FLIPFLOP.circ as structural Verilog: 1 circuit, main circuit main
module main (
  input  in_1,
  input  in_2,
  input  in_3,
  output out_4,
  output out_5
);

  wire nand_1_out, nand_2_out;

  nand nand_1 (nand_1_out, out_5, in_1, in_2);
  nand nand_2 (nand_2_out, in_2, in_3, out_4);
  nand nand_3 (out_4, nand_1_out, out_5);
  nand nand_4 (out_5, out_4, nand_2_out);

  // Notes on the sheet:
  //   SL GOWTHAM
  //   23AD041
endmodule
