// Logisim project MUX.circ as structural Verilog: 1 circuit, main circuit main
module main (
  input  _1,
  input  _0,
  input  D,
  input  _1_2,
  input  D_2,
  input  D_3,
  output Y
);

  wire and_1_out, and_2_out, and_3_out, and_4_out, not_1_out, not_2_out;

  not not_1 (not_1_out, _0);
  not not_2 (not_2_out, _1);
  and and_1 (and_1_out, not_2_out, not_1_out, D);
  and and_2 (and_2_out, not_2_out, _0, _1_2);
  and and_3 (and_3_out, _1, not_1_out, D_2);
  and and_4 (and_4_out, _1, _0, D_3);
  or or_1 (Y, and_1_out, and_2_out, and_3_out, and_4_out);

  // Notes on the sheet:
  //   0
  //   D
  //   2
  //   3
  //   S
  //   SL GOWTHAM
  //   23AD041
  //   S
endmodule
