// Logisim project unit2.circ as structural Verilog: 1 circuit, main circuit main
module main (
  input  in_1,
  input  in_2,
  input  in_3,
  input  in_4,
  input  in_5,
  input  in_6,
  input  in_7
);

  wire and_1_out, and_2_out, and_3_out, and_4_out, and_5_out, not_1_out, or_1_out, or_2_out;

  and and_1 (and_1_out, in_1, in_2);
  and and_2 (and_2_out, in_3, in_4);
  or or_1 (or_1_out, and_1_out, and_2_out);
  LED led_1 (.in(or_1_out));
  LED led_2 (.in(or_1_out));
  and and_3 (and_3_out, in_5, in_6);
  LED led_3 (.in(or_1_out));
  LED led_4 (.in(or_1_out));
  LED led_5 (.in(or_1_out));
  LED led_6 (.in(or_1_out));
  and and_4 (and_4_out, in_7, in_6);
  LED led_7 (.in(or_1_out));
  LED led_8 (.in(or_1_out));
  and and_5 (and_5_out, in_7, in_5);
  or or_2 (or_2_out, and_3_out, and_4_out, and_5_out);
  LED led_9 (.in(not_1_out));
  not not_1 (not_1_out, or_1_out);
  LED led_10 (.in(or_2_out));
  // NOT_Gate not_2 is placed but not wired

  // Notes on the sheet:
  //   Y=AB + CD
  //   Y = AB + BC + CD
  //   DEAVANATHAN.S ☠
endmodule
